# Fritzing sketch Hall_Effect_Sensor (saved by Fritzing 0.9.3b)

parts:
  3-pins_Hall_Effect_Sensor = mystery part, 3 pins [chip_label="Hall Effect Sensor"]
  U3 = ESP32-38PinWide [part_number=ESP32-38PinWide]

nets:
  N1: 3-pins_Hall_Effect_Sensor.pin1, U3.3.3
  N2: 3-pins_Hall_Effect_Sensor.pin2, U3.GND
  N3: 3-pins_Hall_Effect_Sensor.pin3, U3.GPIO34

custom parts:
  ESP32-38PinWide: Generic 38-Pin ESP32 with wide format (only access to one side of pins on a breadboard) based on Stephen Lilley's HiLetgo ESP-WROOM-32 ESP32 ESP-32S Development Board.
